// Logisim project ALU.circ as structural Verilog: 1 circuit, main circuit DC_ALU
module DC_ALU (
  input  [31:0] A,
  input  [31:0] B,
  input  [3:0] ALUOP,
  input  clock,
  output [31:0] OUT
);

  wire comparator_1_eq, comparator_1_gt, comparator_1_lt;
  wire [4:0] bit_extender_1_out, bit_extender_2_out, bit_extender_3_out;
  wire [31:0] adder_1_out, bit_extender_4_out, bit_extender_5_out, bit_extender_6_out, divider_1_out,
       divider_1_rem, multiplier_1_out, negator_1_out, random_1_out, shifter_1_out, shifter_2_out,
       shifter_3_out, subtractor_1_out, xor_1_out;

  Bit_Extender #(.in_width(32), .out_width(5)) bit_extender_1 (.in(B), .out(bit_extender_1_out));
  Bit_Extender #(.in_width(32), .out_width(5)) bit_extender_2 (.in(B), .out(bit_extender_2_out));
  Bit_Extender #(.in_width(32), .out_width(5)) bit_extender_3 (.in(B), .out(bit_extender_3_out));
  Adder #(.width(32)) adder_1 (.a(A), .b(B), .out(adder_1_out));  // open: cin, cout
  Subtractor #(.width(32)) subtractor_1 (.a(A), .b(B), .out(subtractor_1_out));  // open: bin, bout
  Multiplier #(.width(32)) multiplier_1 (.a(A), .b(B), .out(multiplier_1_out));  // open: cin, cout
  Divider #(.width(32)) divider_1 (.a(A), .b(B), .out(divider_1_out), .rem(divider_1_rem));  // open: upper
  Negator #(.width(32)) negator_1 (.in(A), .out(negator_1_out));
  Shifter #(.width(32)) shifter_1 (.in(A), .\dist (bit_extender_1_out), .out(shifter_1_out));
  Shifter #(.width(32), .shift("lr")) shifter_2 (.in(A), .\dist (bit_extender_2_out), .out(shifter_2_out));
  Shifter #(.width(32), .shift("ar")) shifter_3 (.in(A), .\dist (bit_extender_3_out), .out(shifter_3_out));
  Comparator #(.width(32)) comparator_1 (
    .a(A), .b(B), .gt(comparator_1_gt), .eq(comparator_1_eq), .lt(comparator_1_lt));
  assign xor_1_out = A ^ B;  // XOR_Gate xor_1, 32 bits wide
  Random #(.width(32)) random_1 (.clk(clock), .out(random_1_out));  // open: next, clr
  assign bit_extender_4_out = {{31{1'b0}}, comparator_1_gt};  // Bit_Extender bit_extender_4
  assign bit_extender_5_out = {{31{1'b0}}, comparator_1_eq};  // Bit_Extender bit_extender_5
  assign bit_extender_6_out = {{31{1'b0}}, comparator_1_lt};  // Bit_Extender bit_extender_6
  Multiplexer #(.select(4), .width(32), .enable("false")) multiplexer_1 (
    .in0(A), .in1(adder_1_out), .in2(subtractor_1_out), .in3(multiplier_1_out), .in4(divider_1_out),
    .in5(divider_1_rem), .in6(negator_1_out), .in7(shifter_1_out), .in8(shifter_2_out), .in9(shifter_3_out),
    .in10(random_1_out), .in11(bit_extender_5_out), .in12(bit_extender_6_out), .in13(xor_1_out),
    .in14(bit_extender_4_out), .out(OUT), .sel(ALUOP));  // open: in15
endmodule
