// Logisim project CatDust_I.circ as structural Verilog
module main (
  input  [31:0] InstructionIn,
  input  Reset,
  input  ExtMem,
  input  [5:0] FUNC,
  input  [4:0] SHAMT,
  input  [4:0] RD,
  input  [31:0] GPIO_In,
  input  [4:0] RT,
  input  [4:0] RS,
  input  [5:0] OP,
  output [23:0] AdressOut,
  output [31:0] GPIO1,
  output [31:0] GPIO2
);

  wire clock_1_out, comparator_1_eq, comparator_2_eq, comparator_3_eq, forwardingunit_1_enable_plexer,
       jumpcontroller_1_p1, jumpcontroller_1_p4, memorystage_1_selmem, memorystage_1_storemem, mips_ram_1_p7,
       not_1_out, not_2_out, not_3_out, pull_resistor_1_node, registerfile_1_p3;
  wire [1:0] executestage_1_extendfunc, forwardingunit_1_adress_origin_selection, forwardingunit_1_asel,
       forwardingunit_1_bsel;
  wire [3:0] controlled_buffer_1_out, executestage_1_functalu;
  wire [4:0] decodestage_1_decodestage_rd, decodestage_1_decodestage_rs, decodestage_1_decodestage_rt,
       executestage_1_executestage_rdout, executestage_1_rsout, executestage_1_rtout, executestage_1_shamt,
       memorystage_1_memorystage_rdout, registerfile_1_p4;
  wire [5:0] decodestage_1_op, jumpcontroller_1_p5, jumpcontroller_1_p8;
  wire [15:0] decodestage_1_decodestage_imm, executestage_1_ex_imm, memorystage_1_mem_imm, wbstage_1_wb_imm;
  wire [23:0] bit_extender_2_out, memorystage_1_memadressout;
  wire [31:0] bit_extender_1_out, bit_extender_3_out, bit_extender_4_out, bit_extender_5_out,
       bit_extender_6_out, dc_alu_1_out, decodestage_1_decodestage_inst, executestage_1_execute_a,
       executestage_1_execute_b, executestage_1_execute_inst_out, jumpcontroller_1_p3, jumpcontroller_1_p9,
       memorystage_1_a_out, memorystage_1_memdataout, memorystage_1_memory_inst_out,
       memorystage_1_memorystage_aluout, mips_ram_1_p6, multiplexer_1_out, multiplexer_2_out,
       multiplexer_4_out, multiplexer_5_out, multiplexer_6_out, multiplexer_7_out, multiplexer_8_out,
       multiplexer_9_out, registerfile_1_p7, registerfile_1_p8, rom_1_data, wbstage_1_wb_out,
       wbstage_1_wbstage_inst_out;

  Clock clock_1 (.out(clock_1_out));
  Pull_Resistor pull_resistor_1 (.node(pull_resistor_1_node));
  Counter #(.width(24), .max('hffffff)) counter_1 (
    .load(pull_resistor_1_node), .D(bit_extender_2_out), .count(not_1_out), .Q(AdressOut), .clk(clock_1_out),
    .clr(Reset));  // open: carry
  not not_1 (not_1_out, pull_resistor_1_node);
  // Probe on {OP, RS, RT, RD, SHAMT, FUNC}
  // Probe on {OP, RS, RT, RD, SHAMT, FUNC}
  Multiplexer #(.width(32), .enable("false")) multiplexer_1 (
    .in0(rom_1_data), .in1(InstructionIn), .out(multiplexer_1_out), .sel(ExtMem));
  ROM #(.addrWidth(24), .dataWidth(32)) rom_1 (.addr(AdressOut), .data(rom_1_data));  // open: sel
  DecodeStage decodestage_1 (
    .OpIn(multiplexer_1_out), .DecodeStage_Rs(decodestage_1_decodestage_rs),
    .DecodeStage_Rt(decodestage_1_decodestage_rt), .DecodeStage_inst(decodestage_1_decodestage_inst),
    .DecodeStage_Clock(clock_1_out), .DecodeStage_Rd(decodestage_1_decodestage_rd),
    .DecodeStage_IMM(decodestage_1_decodestage_imm), .Flush(jumpcontroller_1_p1), .OP(decodestage_1_op));
  assign bit_extender_1_out = {{8{1'b0}}, AdressOut};  // Bit_Extender bit_extender_1
  Multiplexer #(.width(32), .enable("false")) multiplexer_2 (
    .in0(multiplexer_9_out), .in1(bit_extender_6_out), .out(multiplexer_2_out), .sel(comparator_1_eq));
  Comparator #(.width(6)) comparator_1 (
    .a(wbstage_1_wbstage_inst_out[31:26]), .b(6'b100001), .eq(comparator_1_eq));  // open: gt, lt
  // JumpController jumpcontroller_1: pin names not known; wires that end beside it: jumpcontroller_1_p1, pull_resistor_1_node, jumpcontroller_1_p3, jumpcontroller_1_p4, jumpcontroller_1_p5, decodestage_1_op, decodestage_1_decodestage_imm, jumpcontroller_1_p8, jumpcontroller_1_p9, bit_extender_1_out
  Bit_Extender #(.in_width(32), .out_width(24)) bit_extender_2 (.in(jumpcontroller_1_p3), .out(bit_extender_2_out));
  // RegisterFile registerfile_1: pin names not known; wires that end beside it: multiplexer_2_out, clock_1_out, registerfile_1_p3, registerfile_1_p4, decodestage_1_decodestage_rs, decodestage_1_decodestage_rt, registerfile_1_p7, registerfile_1_p8
  ExecuteStage executestage_1 (
    .Execute_inst_IN(decodestage_1_decodestage_inst), .Execute_inst_out(executestage_1_execute_inst_out),
    .FUNCTALU(executestage_1_functalu), .ExecuteClock(clock_1_out), .Execute_A(executestage_1_execute_a),
    .Execute_B(executestage_1_execute_b), .A_in(registerfile_1_p7), .B_in(registerfile_1_p8),
    .EXTENDFUNC(executestage_1_extendfunc), .ExecuteStage_rdIN(decodestage_1_decodestage_rd),
    .ExecuteStage_RdOUT(executestage_1_executestage_rdout), .RsIn(decodestage_1_decodestage_rs),
    .RtIn(decodestage_1_decodestage_rt), .RsOut(executestage_1_rsout), .RtOut(executestage_1_rtout),
    .EX_IMMIN(decodestage_1_decodestage_imm), .EX_IMM(executestage_1_ex_imm), .Flush(jumpcontroller_1_p4),
    .SHAMT(executestage_1_shamt), .OP(jumpcontroller_1_p5));
  Multiplexer #(.select(2), .width(32)) multiplexer_3 (
    .in0(bit_extender_3_out), .in1(bit_extender_5_out), .in2(bit_extender_6_out), .in3(registerfile_1_p7),
    .out(jumpcontroller_1_p9), .sel(forwardingunit_1_adress_origin_selection),
    .en(forwardingunit_1_enable_plexer));
  assign controlled_buffer_1_out = not_2_out ? executestage_1_functalu : 4'bz;  // Controlled_Buffer controlled_buffer_1
  Comparator #(.width(2)) comparator_2 (
    .a(executestage_1_extendfunc), .b(2'b00), .eq(comparator_2_eq));  // open: gt, lt
  not not_2 (not_2_out, comparator_2_eq);
  ForwardingUnit forwardingunit_1 (
    .Rs2IN(registerfile_1_p4), .RsIn(memorystage_1_memorystage_rdout), .NextRsIN(executestage_1_rsout),
    .NextRtIN(executestage_1_rtout), .ASEL(forwardingunit_1_asel), .BSEL(forwardingunit_1_bsel),
    .stage_3_forward(executestage_1_executestage_rdout), .stage_4_forward(memorystage_1_memorystage_rdout),
    .stage_5_forward(registerfile_1_p4), .\reg (registerfile_1_p4),
    .instruction(decodestage_1_decodestage_inst), .Regfile_out(registerfile_1_p7),
    .adress_origin_selection(forwardingunit_1_adress_origin_selection),
    .enable_plexer(forwardingunit_1_enable_plexer));
  Multiplexer #(.width(32), .enable("false")) multiplexer_4 (
    .in0(memorystage_1_memorystage_aluout), .in1(bit_extender_4_out), .out(multiplexer_4_out),
    .sel(comparator_3_eq));
  Multiplexer #(.select(2), .width(32), .enable("false")) multiplexer_5 (
    .in0(executestage_1_execute_a), .in1(multiplexer_4_out), .in2(multiplexer_7_out),
    .out(multiplexer_5_out), .sel(forwardingunit_1_asel));  // open: in3
  Multiplexer #(.select(2), .width(32), .enable("false")) multiplexer_6 (
    .in0(executestage_1_execute_b), .in1(multiplexer_4_out), .in2(multiplexer_7_out),
    .out(multiplexer_6_out), .sel(forwardingunit_1_bsel));  // open: in3
  Pull_Resistor pull_resistor_2 (.node(controlled_buffer_1_out));
  assign bit_extender_3_out = {{16{1'b0}}, executestage_1_ex_imm};  // Bit_Extender bit_extender_3
  MemoryStage memorystage_1 (
    .Memory_int_IN(executestage_1_execute_inst_out), .Memory_inst_OUT(memorystage_1_memory_inst_out),
    .MemoryStage(clock_1_out), .MemoryStage_RdIn(executestage_1_executestage_rdout),
    .MemoryStage_RdOut(memorystage_1_memorystage_rdout), .memAdressIn(multiplexer_5_out),
    .memAdressOut(memorystage_1_memadressout), .memDataIn(multiplexer_6_out),
    .memDataOut(memorystage_1_memdataout), .MemoryStage_ALUIn(dc_alu_1_out),
    .MemoryStage_ALUOut(memorystage_1_memorystage_aluout), .MEM_IMMIN(executestage_1_ex_imm),
    .MEM_IMM(memorystage_1_mem_imm), .SELMem(memorystage_1_selmem), .StoreMem(memorystage_1_storemem),
    .A_in(executestage_1_execute_a), .A_out(memorystage_1_a_out));  // open: Flush
  Comparator #(.width(6)) comparator_3 (.a(jumpcontroller_1_p5), .b(6'b011010), .eq(comparator_3_eq));  // open: gt, lt
  DC_ALU dc_alu_1 (
    .A(multiplexer_5_out), .B(multiplexer_6_out), .clock(clock_1_out), .OUT(dc_alu_1_out),
    .ALUOP(controlled_buffer_1_out));
  jumpComparator jumpcomparator_1 (
    .A(multiplexer_5_out), .A_2(multiplexer_6_out), .op(jumpcontroller_1_p5), .Status_bit(jumpcontroller_1_p8));
  Pull_Resistor pull_resistor_3 (.node(memorystage_1_storemem));
  assign bit_extender_4_out = {{16{1'b0}}, memorystage_1_mem_imm};  // Bit_Extender bit_extender_4
  not not_3 (not_3_out, memorystage_1_storemem);
  Multiplexer #(.width(32), .enable("false")) multiplexer_7 (
    .in0(wbstage_1_wb_out), .in1(bit_extender_6_out), .out(multiplexer_7_out), .sel(comparator_3_eq));
  // MIPS_RAM mips_ram_1: pin names not known; wires that end beside it: memorystage_1_memadressout, memorystage_1_memdataout, memorystage_1_storemem, clock_1_out, not_3_out, mips_ram_1_p6, mips_ram_1_p7
  WBStage wbstage_1 (
    .WBStage_inst_In(memorystage_1_memory_inst_out), .WBClock(clock_1_out),
    .WBStage_inst_Out(wbstage_1_wbstage_inst_out), .WB_memIn(multiplexer_8_out), .WB_Out(wbstage_1_wb_out),
    .WB_RdIn(memorystage_1_memorystage_rdout), .WB_RdOut(registerfile_1_p4),
    .WBStage_WBEnable(registerfile_1_p3), .WB_IMMIN(memorystage_1_mem_imm), .WB_IMM(wbstage_1_wb_imm),
    .A_in(memorystage_1_a_out), .B_in(memorystage_1_memdataout), .GPIO_Out_1(GPIO1), .GPIO_Out_2(GPIO2));  // open: WB_ConstIn, Flush
  Multiplexer #(.width(32), .enable("false")) multiplexer_8 (
    .in0(memorystage_1_memorystage_aluout), .in1(mips_ram_1_p6), .out(multiplexer_8_out),
    .sel(memorystage_1_selmem));
  assign bit_extender_5_out = {{16{1'b0}}, memorystage_1_mem_imm};  // Bit_Extender bit_extender_5
  Multiplexer #(.width(32), .enable("false")) multiplexer_9 (
    .in0(wbstage_1_wb_out), .in1(GPIO_In), .out(multiplexer_9_out), .sel(mips_ram_1_p7));
  assign bit_extender_6_out = {{16{1'b0}}, wbstage_1_wb_imm};  // Bit_Extender bit_extender_6

  // Notes on the sheet:
  //   contents of rom_1 (hex, n*v repeats v):
  //   87000000 87200006 b3380000 87000000 a3180000 87200001 b3190000 87000001 85000008 85200001 a1290000
  //   1094003 85200000 a1290000 85400005 12a4803 1094001 8520000a 1094001 85200007 1094001 b1180000
  //   87000002 87206f3b b3380000 87000003 87200000 b3380000 85000003 a1080000 8520000a 85400026 68084800
  //   2d400000 8540002d 3d400000 85000000 a1280000 b1280000 8500001d 3d000000
endmodule

module Counter32 (
  input  [31:0] IN,
  input  LOAD,
  input  CLOCK,
  input  RESET,
  output [31:0] OUT
);

  wire [31:0] adder_1_out, multiplexer_1_out;

  Adder #(.width(32)) adder_1 (.a(OUT), .b(32'h4), .out(adder_1_out));  // open: cin, cout
  Multiplexer #(.width(32), .enable("false")) multiplexer_1 (
    .in0(adder_1_out), .in1(IN), .out(multiplexer_1_out), .sel(LOAD));
  Register #(.width(32)) register_1 (.D(multiplexer_1_out), .Q(OUT), .clk(CLOCK), .clr(RESET));  // open: en
endmodule

module InstructionDecoder (
  input  [31:0] in_1,
  output [5:0] FUNC,
  output [4:0] SHAMT,
  output [4:0] RD,
  output [4:0] RT,
  output [4:0] RS,
  output [5:0] OP,
  output [15:0] Immediate,
  output [25:0] Address,
  output Wenable
);

  wire comparator_1_eq, comparator_2_eq;

  Comparator #(.width(32)) comparator_1 (.a({32{1'b0}}), .b(in_1), .eq(comparator_1_eq));  // open: gt, lt
  Comparator #(.width(6)) comparator_2 (.a(in_1[31:26]), .b({6{1'b0}}), .eq(comparator_2_eq));  // open: gt, lt
  and and_1 (Wenable, ~comparator_1_eq, comparator_2_eq);  // AND_Gate

  assign Address = in_1[25:0];
  assign FUNC = in_1[5:0];
  assign Immediate = in_1[15:0];
  assign OP = in_1[31:26];
  assign RD = in_1[15:11];
  assign RS = in_1[25:21];
  assign RT = in_1[20:16];
  assign SHAMT = in_1[10:6];

  // Notes on the sheet:
  //   write register when op = 000000
  //   R TYPE
endmodule

module DecodeStage (
  input  [31:0] OpIn,
  input  Flush,
  input  DecodeStage_Clock,
  output [31:0] DecodeStage_inst,
  output [4:0] DecodeStage_Rt,
  output [4:0] DecodeStage_Rs,
  output [4:0] DecodeStage_Rd,
  output [15:0] DecodeStage_IMM,
  output [5:0] OP
);

  wire comparator_1_eq;
  wire [4:0] instructiondecoder_1_rd, instructiondecoder_1_rs, instructiondecoder_1_rt, register_4_q;
  wire [5:0] instructiondecoder_1_op, register_6_q;
  wire [15:0] instructiondecoder_1_immediate;

  InstructionDecoder instructiondecoder_1 (
    .in_1(OpIn), .RD(instructiondecoder_1_rd), .RT(instructiondecoder_1_rt), .RS(instructiondecoder_1_rs),
    .OP(instructiondecoder_1_op), .Immediate(instructiondecoder_1_immediate));  // open: FUNC, SHAMT, Address, Wenable
  Register #(.width(32)) register_1 (.D(OpIn), .Q(DecodeStage_inst), .clk(DecodeStage_Clock), .clr(Flush));  // open: en
  Register #(.width(5)) register_2 (
    .D(instructiondecoder_1_rt), .Q(DecodeStage_Rt), .clk(DecodeStage_Clock), .clr(Flush));  // open: en
  Register #(.width(5)) register_3 (
    .D(instructiondecoder_1_rs), .Q(DecodeStage_Rs), .clk(DecodeStage_Clock), .clr(Flush));  // open: en
  Register #(.width(5)) register_4 (
    .D(instructiondecoder_1_rd), .Q(register_4_q), .clk(DecodeStage_Clock), .clr(Flush));  // open: en
  Register #(.width(16)) register_5 (
    .D(instructiondecoder_1_immediate), .Q(DecodeStage_IMM), .clk(DecodeStage_Clock), .clr(Flush));  // open: en
  Register #(.width(6)) register_6 (
    .D(instructiondecoder_1_op), .Q(register_6_q), .clk(DecodeStage_Clock), .clr(Flush));  // open: en
  Register #(.width(6)) register_7 (
    .D(instructiondecoder_1_op), .Q(OP), .clk(DecodeStage_Clock), .clr(Flush));  // open: en
  Comparator #(.width(6)) comparator_1 (.a(register_6_q), .b(6'b100001), .eq(comparator_1_eq));  // open: gt, lt
  Multiplexer #(.width(5), .enable("false")) multiplexer_1 (
    .in0(register_4_q), .in1(DecodeStage_Rs), .out(DecodeStage_Rd), .sel(comparator_1_eq));
endmodule

module ExecuteStage (
  input  [31:0] Execute_inst_IN,
  input  ExecuteClock,
  input  [31:0] A_in,
  input  [31:0] B_in,
  input  [4:0] ExecuteStage_rdIN,
  input  [4:0] RsIn,
  input  [4:0] RtIn,
  input  [15:0] EX_IMMIN,
  input  Flush,
  output [31:0] Execute_inst_out,
  output [3:0] FUNCTALU,
  output [1:0] EXTENDFUNC,
  output [5:0] OP,
  output [4:0] SHAMT,
  output [31:0] Execute_A,
  output [31:0] Execute_B,
  output [4:0] ExecuteStage_RdOUT,
  output [4:0] RsOut,
  output [4:0] RtOut,
  output [15:0] EX_IMM
);

  wire instructiondecoder_1_wenable;
  wire [4:0] instructiondecoder_1_shamt;
  wire [5:0] instructiondecoder_1_func, instructiondecoder_1_op, pull_resistor_1_node;

  InstructionDecoder instructiondecoder_1 (
    .in_1(Execute_inst_IN), .FUNC(instructiondecoder_1_func), .SHAMT(instructiondecoder_1_shamt),
    .OP(instructiondecoder_1_op), .Wenable(instructiondecoder_1_wenable));  // open: RD, RT, RS, Immediate, Address
  Pull_Resistor pull_resistor_1 (.node(pull_resistor_1_node));
  assign pull_resistor_1_node = instructiondecoder_1_wenable ? instructiondecoder_1_func : 6'bz;  // Controlled_Buffer controlled_buffer_1
  Register #(.width(32)) register_1 (
    .D(Execute_inst_IN), .Q(Execute_inst_out), .clk(ExecuteClock), .clr(Flush));  // open: en
  Register #(.width(6)) register_2 (
    .D(pull_resistor_1_node), .Q({EXTENDFUNC, FUNCTALU}), .clk(ExecuteClock), .clr(Flush));  // open: en
  Register #(.width(6)) register_3 (.D(instructiondecoder_1_op), .Q(OP), .clk(ExecuteClock), .clr(Flush));  // open: en
  Register #(.width(5)) register_4 (
    .D(instructiondecoder_1_shamt), .Q(SHAMT), .clk(ExecuteClock), .clr(Flush));  // open: en
  Register #(.width(32)) register_5 (.D(A_in), .Q(Execute_A), .clk(ExecuteClock), .clr(Flush));  // open: en
  Register #(.width(32)) register_6 (.D(B_in), .Q(Execute_B), .clk(ExecuteClock), .clr(Flush));  // open: en
  Register #(.width(5)) register_7 (
    .D(ExecuteStage_rdIN), .Q(ExecuteStage_RdOUT), .clk(ExecuteClock), .clr(Flush));  // open: en
  Register #(.width(5)) register_8 (.D(RsIn), .Q(RsOut), .clk(ExecuteClock), .clr(Flush));  // open: en
  Register #(.width(5)) register_9 (.D(RtIn), .Q(RtOut), .clk(ExecuteClock), .clr(Flush));  // open: en
  Register #(.width(16)) register_10 (.D(EX_IMMIN), .Q(EX_IMM), .clk(ExecuteClock), .clr(Flush));  // open: en
endmodule

module MemoryStage (
  input  MemoryStage,
  input  [31:0] Memory_int_IN,
  input  [4:0] MemoryStage_RdIn,
  input  [31:0] memAdressIn,
  input  [31:0] memDataIn,
  input  [31:0] MemoryStage_ALUIn,
  input  [15:0] MEM_IMMIN,
  input  [31:0] A_in,
  input  Flush,
  output [31:0] Memory_inst_OUT,
  output SELMem,
  output [4:0] MemoryStage_RdOut,
  output StoreMem,
  output [23:0] memAdressOut,
  output [31:0] memDataOut,
  output [31:0] MemoryStage_ALUOut,
  output [15:0] MEM_IMM,
  output [31:0] A_out
);

  wire comparator_1_eq;
  wire [23:0] bit_extender_1_out;

  Bit_Extender #(.in_width(32), .out_width(24)) bit_extender_1 (.in(memAdressIn), .out(bit_extender_1_out));
  Register #(.width(32)) register_1 (
    .D(Memory_int_IN), .Q(Memory_inst_OUT), .clk(MemoryStage), .clr(Flush));  // open: en
  Register #(.width(5)) register_2 (
    .D(MemoryStage_RdIn), .Q(MemoryStage_RdOut), .clk(MemoryStage), .clr(Flush));  // open: en
  Register #(.width(24)) register_3 (
    .D(bit_extender_1_out), .Q(memAdressOut), .clk(MemoryStage), .clr(Flush));  // open: en
  Register #(.width(32)) register_4 (.D(memDataIn), .Q(memDataOut), .clk(MemoryStage), .clr(Flush));  // open: en
  Register #(.width(32)) register_5 (
    .D(MemoryStage_ALUIn), .Q(MemoryStage_ALUOut), .clk(MemoryStage), .clr(Flush));  // open: en
  Register #(.width(16)) register_6 (.D(MEM_IMMIN), .Q(MEM_IMM), .clk(MemoryStage), .clr(Flush));  // open: en
  Register #(.width(32)) register_7 (.D(A_in), .Q(A_out), .clk(MemoryStage), .clr(Flush));  // open: en
  Pull_Resistor pull_resistor_1 (.node(Flush));
  Comparator #(.width(3)) comparator_1 (.a(3'b101), .b(Memory_inst_OUT[31:29]), .eq(comparator_1_eq));  // open: gt, lt
  and and_1 (StoreMem, comparator_1_eq, Memory_inst_OUT[28]);
  and and_2 (SELMem, comparator_1_eq, ~StoreMem);  // AND_Gate
endmodule

module WBStage (
  input  WBClock,
  input  [31:0] A_in,
  input  [31:0] WBStage_inst_In,
  input  [31:0] WB_ConstIn,
  input  [31:0] WB_memIn,
  input  [4:0] WB_RdIn,
  input  [15:0] WB_IMMIN,
  input  [31:0] B_in,
  input  Flush,
  output [31:0] GPIO_Out_1,
  output [31:0] WBStage_inst_Out,
  output WBStage_WBEnable,
  output [31:0] WB_Out,
  output [4:0] WB_RdOut,
  output [15:0] WB_IMM,
  output [31:0] GPIO_Out_2
);

  wire comparator_1_eq, comparator_2_eq, comparator_3_eq, comparator_4_eq, or_1_out;
  wire [31:0] register_3_q, register_4_q;

  Pull_Resistor pull_resistor_1 (.node(Flush));
  Register #(.width(32)) register_1 (.D(A_in), .Q(GPIO_Out_1), .clk(WBClock), .clr(Flush));  // open: en
  Register #(.width(32)) register_2 (
    .D(WBStage_inst_In), .Q(WBStage_inst_Out), .clk(WBClock), .clr(Flush));  // open: en
  Register #(.width(32)) register_3 (.D(WB_ConstIn), .Q(register_3_q), .clk(WBClock), .clr(Flush));  // open: en
  Register #(.width(32)) register_4 (.D(WB_memIn), .Q(register_4_q), .clk(WBClock), .clr(Flush));  // open: en
  Register #(.width(5)) register_5 (.D(WB_RdIn), .Q(WB_RdOut), .clk(WBClock), .clr(Flush));  // open: en
  Register #(.width(16)) register_6 (.D(WB_IMMIN), .Q(WB_IMM), .clk(WBClock), .clr(Flush));  // open: en
  Register #(.width(32)) register_7 (.D(B_in), .Q(GPIO_Out_2), .clk(WBClock), .clr(Flush));  // open: en
  Comparator #(.width(6)) comparator_1 (
    .a(WBStage_inst_Out[31:26]), .b(6'b100001), .eq(comparator_1_eq));  // open: gt, lt
  Multiplexer #(.width(32), .enable("false")) multiplexer_1 (
    .in0(register_4_q), .in1(register_3_q), .out(WB_Out), .sel(comparator_1_eq));
  Comparator #(.width(5)) comparator_2 (.a(WB_RdOut), .b({5{1'b0}}), .eq(comparator_2_eq));  // open: gt, lt
  Comparator #(.width(6)) comparator_3 (
    .a(WBStage_inst_Out[31:26]), .b({6{1'b0}}), .eq(comparator_3_eq));  // open: gt, lt
  Comparator #(.width(6)) comparator_4 (
    .a(WBStage_inst_Out[31:26]), .b(6'b100001), .eq(comparator_4_eq));  // open: gt, lt
  or or_1 (or_1_out, comparator_3_eq, comparator_4_eq);
  and and_1 (WBStage_WBEnable, or_1_out, ~comparator_2_eq);  // AND_Gate
endmodule

module ForwardingUnit (
  input  [4:0] RsIn,
  input  [4:0] Rs2IN,
  input  [4:0] NextRsIN,
  input  [4:0] NextRtIN,
  input  [4:0] stage_3_forward,
  input  [4:0] stage_4_forward,
  input  [4:0] stage_5_forward,
  input  [4:0] \reg ,
  input  [31:0] instruction,
  input  [31:0] Regfile_out,
  output [1:0] ASEL,
  output [1:0] BSEL,
  output [1:0] adress_origin_selection,
  output enable_plexer
);

  wire comparator_1_eq, comparator_2_eq, comparator_3_eq, comparator_4_eq, comparator_5_eq, comparator_6_eq,
       comparator_7_eq, comparator_8_eq, comparator_9_eq, comparator_10_eq, comparator_11_eq,
       comparator_12_eq, not_1_out, not_2_out, not_3_out;
  wire [1:0] priority_encoder_1_out;

  Comparator #(.width(5)) comparator_1 (.a(stage_5_forward), .b(\reg ), .eq(comparator_1_eq));  // open: gt, lt
  Comparator #(.width(32)) comparator_2 (.a(Regfile_out), .b({32{1'b0}}), .eq(comparator_2_eq));  // open: gt, lt
  not not_1 (not_1_out, comparator_2_eq);
  Comparator #(.width(5)) comparator_3 (.a(RsIn), .b(NextRsIN), .eq(comparator_3_eq));  // open: gt, lt
  Comparator #(.width(5)) comparator_4 (.a(Rs2IN), .b(NextRsIN), .eq(comparator_4_eq));  // open: gt, lt
  Comparator #(.width(5)) comparator_5 (.a(RsIn), .b(NextRtIN), .eq(comparator_5_eq));  // open: gt, lt
  Comparator #(.width(5)) comparator_6 (.a(Rs2IN), .b(NextRtIN), .eq(comparator_6_eq));  // open: gt, lt
  Comparator #(.width(5)) comparator_7 (.a(\reg ), .b(stage_3_forward), .eq(comparator_7_eq));  // open: gt, lt
  Comparator #(.width(5)) comparator_8 (.a(\reg ), .b(stage_4_forward), .eq(comparator_8_eq));  // open: gt, lt
  Comparator #(.width(3)) comparator_9 (.a(instruction[31:29]), .b(3'b001), .eq(comparator_9_eq));  // open: gt, lt
  Comparator #(.width(3)) comparator_10 (.a(3'b010), .b(instruction[31:29]), .eq(comparator_10_eq));  // open: gt, lt
  not not_2 (not_2_out, comparator_11_eq);
  Comparator #(.width(5)) comparator_11 (.a(RsIn), .b({5{1'b0}}), .eq(comparator_11_eq));  // open: gt, lt
  not not_3 (not_3_out, comparator_12_eq);
  Comparator #(.width(5)) comparator_12 (.a(Rs2IN), .b({5{1'b0}}), .eq(comparator_12_eq));  // open: gt, lt
  Priority_Encoder #(.select(2)) priority_encoder_1 (
    .in0(comparator_7_eq), .in1(comparator_8_eq), .in2(comparator_1_eq), .in3(not_1_out),
    .out(priority_encoder_1_out));  // open: gs, en_out, en_in
  or or_1 (enable_plexer, comparator_9_eq, comparator_10_eq);
  assign adress_origin_selection = enable_plexer ? priority_encoder_1_out : 2'bz;  // Controlled_Buffer controlled_buffer_1
  Pull_Resistor pull_resistor_1 (.node(adress_origin_selection));
  assign ASEL[1] = not_3_out ? comparator_4_eq : 1'bz;  // Controlled_Buffer controlled_buffer_2
  assign BSEL[1] = not_3_out ? comparator_6_eq : 1'bz;  // Controlled_Buffer controlled_buffer_3
  Pull_Resistor pull_resistor_2 (.node(ASEL[1]));
  Pull_Resistor pull_resistor_3 (.node(BSEL[1]));
  Pull_Resistor pull_resistor_4 (.node(ASEL[0]));
  assign ASEL[0] = not_2_out ? comparator_3_eq : 1'bz;  // Controlled_Buffer controlled_buffer_4
  Pull_Resistor pull_resistor_5 (.node(BSEL[0]));
  assign BSEL[0] = not_2_out ? comparator_5_eq : 1'bz;  // Controlled_Buffer controlled_buffer_5
endmodule

module JumpController (
  input  [5:0] COMPFLAG,
  input  [5:0] OP,
  input  [31:0] CurentAdress,
  input  [15:0] IMM,
  input  [31:0] A,
  input  [31:0] InterruptAdress,
  input  InterruptEnable,
  output FlushID,
  output FlushEX,
  output LOAD,
  output [31:0] ADRESS
);

  wire comparator_1_eq, comparator_2_eq, or_1_out;
  wire [2:0] controlled_buffer_1_out;
  wire [31:0] adder_1_out, bit_extender_1_out, multiplexer_1_out;

  assign bit_extender_1_out = {{16{1'b0}}, IMM};  // Bit_Extender bit_extender_1
  Multiplexer #(.width(32), .enable("false")) multiplexer_1 (
    .in0(A), .in1(InterruptAdress), .out(multiplexer_1_out), .sel(InterruptEnable));
  Pull_Resistor pull_resistor_1 (.node(InterruptEnable));
  Comparator #(.width(3)) comparator_1 (.a(3'b001), .b(OP[5:3]), .eq(comparator_1_eq));  // open: gt, lt
  or or_1 (or_1_out, comparator_1_eq, comparator_2_eq);
  assign controlled_buffer_1_out = or_1_out ? OP[2:0] : 3'bz;  // Controlled_Buffer controlled_buffer_1
  Comparator #(.width(3)) comparator_2 (.a(OP[5:3]), .b(3'b010), .eq(comparator_2_eq));  // open: gt, lt
  Adder #(.width(32)) adder_1 (.a(CurentAdress), .b(bit_extender_1_out), .out(adder_1_out));  // open: cin, cout
  Multiplexer #(.width(32), .enable("false")) multiplexer_2 (
    .in0(multiplexer_1_out), .in1(adder_1_out), .out(ADRESS), .sel(comparator_2_eq));
  Multiplexer #(.select(3), .enable("false")) multiplexer_3 (
    .in0(1'b0), .in1(COMPFLAG[0]), .in2(COMPFLAG[1]), .in3(COMPFLAG[2]), .in4(COMPFLAG[3]),
    .in5(COMPFLAG[4]), .in6(COMPFLAG[5]), .in7(1'b1), .out(LOAD), .sel(controlled_buffer_1_out));
  Pull_Resistor pull_resistor_2 (.node(controlled_buffer_1_out));

  assign FlushEX = 1'b0;
  assign FlushID = 1'b0;
endmodule

module jumpComparator (
  input  [31:0] A,
  input  [31:0] A_2,
  input  [5:0] op,
  output [5:0] Status_bit
);

  wire comparator_1_eq;
  wire [5:0] comparator_2_gt;

  Comparator #(.width(6)) comparator_1 (.a(op), .b(6'b011010), .eq(comparator_1_eq));  // open: gt, lt
  Comparator #(.width(32)) comparator_2 (
    .a(A), .b(A_2), .gt(comparator_2_gt[0]), .eq(comparator_2_gt[1]), .lt(comparator_2_gt[2]));
  not not_1 (comparator_2_gt[4], comparator_2_gt[1]);
  or or_1 (comparator_2_gt[3], comparator_2_gt[0], comparator_2_gt[1]);
  or or_2 (comparator_2_gt[5], comparator_2_gt[1], comparator_2_gt[2]);
  Register #(.width(6)) register_1 (.D(comparator_2_gt), .Q(Status_bit), .clk(comparator_1_eq));  // open: en, clr
endmodule
