// Logisim project CatDust_I_MIPS.circ as structural Verilog: 5 circuits, main circuit main
module main (
  input  in_1,
  input  in_2
);

  wire clock_1_out, registerfile_1_p1, registerfile_1_p4, registerfile_1_p6;
  wire [4:0] decodestage_1_decodestage_rs, decodestage_1_decodestage_rt, executestage_1_functalu;
  wire [31:0] counter32_1_out, decodestage_1_decodestage_op, executestage_1_execute_a,
       executestage_1_execute_b, mipsprogramrom_1_p2, registerfile_1_p10, registerfile_1_p11, undriven;

  Clock clock_1 (.out(clock_1_out));
  Counter32 counter32_1 (.IN(undriven), .LOAD(in_2), .CLOCK(clock_1_out), .OUT(counter32_1_out), .RESET(in_1));
  // MIPSProgramROM mipsprogramrom_1: pin names not known; wires that end beside it: counter32_1_out, mipsprogramrom_1_p2
  DecodeStage decodestage_1 (
    .OpIn(mipsprogramrom_1_p2), .DecodeStage_Rs(decodestage_1_decodestage_rs),
    .DecodeStage_Rt(decodestage_1_decodestage_rt), .DecodeStage_OP(decodestage_1_decodestage_op),
    .DecodeStage_Clock(clock_1_out));
  // RegisterFile registerfile_1: pin names not known; wires that end beside it: registerfile_1_p1, registerfile_1_p1, clock_1_out, registerfile_1_p4, registerfile_1_p4, registerfile_1_p6, registerfile_1_p6, decodestage_1_decodestage_rs, decodestage_1_decodestage_rt, registerfile_1_p10, registerfile_1_p11
  ExecuteStage executestage_1 (
    .Execute_OPIN(decodestage_1_decodestage_op), .FUNCTALU(executestage_1_functalu),
    .ExecuteClock(clock_1_out), .Execute_A(executestage_1_execute_a), .Execute_B(executestage_1_execute_b),
    .A_in(registerfile_1_p10), .B_in(registerfile_1_p11));  // open: Execute_OPOUT, EXTENDFUNC
  // Mips_ALU mips_alu_1: pin names not known; wires that end beside it: executestage_1_execute_a, executestage_1_execute_b, executestage_1_functalu
  // MIPS_RAM mips_ram_1: pin names not known; wires that end beside it: clock_1_out
endmodule

module Counter32 (
  input  [31:0] IN,
  input  LOAD,
  input  CLOCK,
  input  RESET,
  output [31:0] OUT
);

  wire [31:0] adder_1_out, multiplexer_1_out;

  Adder #(.width(32)) adder_1 (.a(OUT), .b(32'h4), .out(adder_1_out));  // open: cin, cout
  Multiplexer #(.width(32), .enable("false")) multiplexer_1 (
    .in0(adder_1_out), .in1(IN), .out(multiplexer_1_out), .sel(LOAD));
  Register #(.width(32)) register_1 (.D(multiplexer_1_out), .Q(OUT), .clk(CLOCK), .clr(RESET));  // open: en
endmodule

module InstructionDecoder (
  input  [31:0] in_1,
  output [5:0] FUNC,
  output [4:0] SHAMT,
  output [4:0] RD,
  output [4:0] RT,
  output [4:0] RS,
  output [5:0] OP,
  output [15:0] Immediate,
  output [25:0] Address,
  output Wenable
);

  wire comparator_1_eq, comparator_2_eq;

  Comparator #(.width(32)) comparator_1 (.a({32{1'b0}}), .b(in_1), .eq(comparator_1_eq));  // open: gt, lt
  Comparator #(.width(6)) comparator_2 (.a(in_1[31:26]), .b({6{1'b0}}), .eq(comparator_2_eq));  // open: gt, lt
  and and_1 (Wenable, ~comparator_1_eq, comparator_2_eq);  // AND_Gate

  assign Address = in_1[25:0];
  assign FUNC = in_1[5:0];
  assign Immediate = in_1[15:0];
  assign OP = in_1[31:26];
  assign RD = in_1[15:11];
  assign RS = in_1[25:21];
  assign RT = in_1[20:16];
  assign SHAMT = in_1[10:6];

  // Notes on the sheet:
  //   R TYPE
endmodule

module DecodeStage (
  input  [31:0] OpIn,
  input  DecodeStage_Clock,
  output [31:0] DecodeStage_OP,
  output [4:0] DecodeStage_Rt,
  output [4:0] DecodeStage_Rs
);

  wire [4:0] instructiondecoder_1_rs, instructiondecoder_1_rt;

  InstructionDecoder instructiondecoder_1 (
    .in_1(OpIn), .RT(instructiondecoder_1_rt), .RS(instructiondecoder_1_rs));  // open: FUNC, SHAMT, RD, OP, Immediate, Address, Wenable
  Register #(.width(32)) register_1 (.D(OpIn), .Q(DecodeStage_OP), .clk(DecodeStage_Clock));  // open: en, clr
  Register #(.width(5)) register_2 (
    .D(instructiondecoder_1_rt), .Q(DecodeStage_Rt), .clk(DecodeStage_Clock));  // open: en, clr
  Register #(.width(5)) register_3 (
    .D(instructiondecoder_1_rs), .Q(DecodeStage_Rs), .clk(DecodeStage_Clock));  // open: en, clr
endmodule

module ExecuteStage (
  input  [31:0] Execute_OPIN,
  input  ExecuteClock,
  input  [31:0] A_in,
  input  [31:0] B_in,
  output [31:0] Execute_OPOUT,
  output [4:0] FUNCTALU,
  output EXTENDFUNC,
  output [31:0] Execute_A,
  output [31:0] Execute_B
);

  wire instructiondecoder_1_wenable;
  wire [5:0] instructiondecoder_1_func, pull_resistor_1_node;

  InstructionDecoder instructiondecoder_1 (
    .in_1(Execute_OPIN), .FUNC(instructiondecoder_1_func), .Wenable(instructiondecoder_1_wenable));  // open: SHAMT, RD, RT, RS, OP, Immediate, Address
  Pull_Resistor pull_resistor_1 (.node(pull_resistor_1_node));
  assign pull_resistor_1_node = instructiondecoder_1_wenable ? instructiondecoder_1_func : 6'bz;  // Controlled_Buffer controlled_buffer_1
  Register #(.width(32)) register_1 (.D(Execute_OPIN), .Q(Execute_OPOUT), .clk(ExecuteClock));  // open: en, clr
  Register #(.width(6)) register_2 (
    .D(pull_resistor_1_node), .Q({EXTENDFUNC, FUNCTALU}), .clk(ExecuteClock));  // open: en, clr
  Register #(.width(32)) register_3 (.D(A_in), .Q(Execute_A), .clk(ExecuteClock));  // open: en, clr
  Register #(.width(32)) register_4 (.D(B_in), .Q(Execute_B), .clk(ExecuteClock));  // open: en, clr
endmodule
